// Logisim project alu.circ as structural Verilog: 3 circuits, main circuit main
module main (
  input  A,
  input  B,
  input  C,
  output sum_out,
  output out_5
);

  wire and_1_out, and_2_out, xor_1_out;

  xor xor_1 (xor_1_out, A, B);
  and and_1 (and_1_out, A, B);
  xor xor_2 (sum_out, xor_1_out, C);
  and and_2 (and_2_out, xor_1_out, C);
  or or_1 (out_5, and_1_out, and_2_out);

  // Notes on the sheet:
  //   s
  //   carry
  //   carry_out
endmodule

module adder4 (
  input  in_1,
  input  in_2,
  input  in_3,
  input  in_4,
  input  in_5,
  input  in_6,
  input  in_7,
  input  in_8,
  input  in_9,
  output out_10,
  output out_11,
  output out_12,
  output out_13
);

  wire adder_1_cout, adder_2_cout, adder_3_cout;

  Adder #(.width(1)) adder_1 (.a(in_2), .b(in_3), .out(out_10), .cin(in_1), .cout(adder_1_cout));
  Adder #(.width(1)) adder_2 (.a(in_4), .b(in_5), .out(out_11), .cin(adder_1_cout), .cout(adder_2_cout));
  Adder #(.width(1)) adder_3 (.a(in_6), .b(in_7), .out(out_12), .cin(adder_2_cout), .cout(adder_3_cout));
  Adder #(.width(1)) adder_4 (.a(in_8), .b(in_9), .out(out_13), .cin(adder_3_cout));  // open: cout
endmodule

module _4bits (
  input  in_1,
  input  [3:0] A,
  input  [3:0] B,
  input  in_4
);

  wire [3:0] adder_1_out, bit_extender_1_out, xor_1_out;

  assign bit_extender_1_out = {{3{1'b0}}, in_4};  // Bit_Extender bit_extender_1
  Adder #(.width(4)) adder_1 (.a(A), .b(xor_1_out), .out(adder_1_out), .cin(in_1));  // open: cout
  assign xor_1_out = B ^ bit_extender_1_out;  // XOR_Gate xor_1, 4 bits wide
  Hex_Digit_Display hex_digit_display_1 (.value(adder_1_out));  // open: dp
endmodule
