// Logisim project cpuNotcomplet.circ as structural Verilog: 5 circuits, main circuit main
module main (
);

  Regfil regfil_1 ();  // open: inpu, clk, OutputRegAselect, OutputRegBselect, InpuREGselect, A, B
  alu1 alu1_1 ();  // open: A, B, op, o
endmodule

module adder4 (
  input  in_1,
  input  in_2,
  input  in_3,
  input  in_4,
  input  in_5,
  input  in_6,
  input  in_7,
  input  in_8,
  input  in_9,
  output out_10,
  output out_11,
  output out_12,
  output out_13
);

  wire adder_1_cout, adder_2_cout, adder_3_cout;

  Adder #(.width(1)) adder_1 (.a(in_2), .b(in_3), .out(out_10), .cin(in_1), .cout(adder_1_cout));
  Adder #(.width(1)) adder_2 (.a(in_4), .b(in_5), .out(out_11), .cin(adder_1_cout), .cout(adder_2_cout));
  Adder #(.width(1)) adder_3 (.a(in_6), .b(in_7), .out(out_12), .cin(adder_2_cout), .cout(adder_3_cout));
  Adder #(.width(1)) adder_4 (.a(in_8), .b(in_9), .out(out_13), .cin(adder_3_cout));  // open: cout
endmodule

module L_4bits_809183f8 (
  input  in_1,
  input  [3:0] A,
  input  [3:0] B,
  input  in_4
);

  wire [3:0] adder_1_out, bit_extender_1_out, xor_1_out;

  assign bit_extender_1_out = {{3{in_4}}, in_4};  // Bit_Extender bit_extender_1
  Adder #(.width(4)) adder_1 (.a(A), .b(xor_1_out), .out(adder_1_out), .cin(in_1));  // open: cout
  assign xor_1_out = B ^ bit_extender_1_out;  // XOR_Gate xor_1, 4 bits wide
  Hex_Digit_Display hex_digit_display_1 (.value(adder_1_out));  // open: dp
endmodule

module Regfil (
  input  [3:0] inpu,
  input  clk,
  input  [2:0] OutputRegAselect,
  input  [2:0] OutputRegBselect,
  input  [2:0] InpuREGselect,
  output [3:0] A,
  output [3:0] B
);

  wire demultiplexer_1_out0, demultiplexer_1_out1, demultiplexer_1_out2, demultiplexer_1_out3,
       demultiplexer_1_out4, demultiplexer_1_out5, demultiplexer_1_out6, demultiplexer_1_out7;
  wire [3:0] R0_q, R1_q, R2_q, R3_q, R4_q, R5_q, R6_q, R7_q;

  Demultiplexer #(.select(3)) demultiplexer_1 (
    .out0(demultiplexer_1_out0), .out1(demultiplexer_1_out1), .out2(demultiplexer_1_out2),
    .out3(demultiplexer_1_out3), .out4(demultiplexer_1_out4), .out5(demultiplexer_1_out5),
    .out6(demultiplexer_1_out6), .out7(demultiplexer_1_out7), .in(1'b1), .sel(InpuREGselect));
  Register #(.width(4)) R0 (.D(inpu), .en(demultiplexer_1_out0), .clk(clk), .Q(R0_q));  // open: clr
  Register #(.width(4)) R1 (.D(inpu), .en(demultiplexer_1_out1), .clk(clk), .Q(R1_q));  // open: clr
  Register #(.width(4)) R2 (.D(inpu), .en(demultiplexer_1_out2), .clk(clk), .Q(R2_q));  // open: clr
  Register #(.width(4)) R3 (.D(inpu), .en(demultiplexer_1_out3), .clk(clk), .Q(R3_q));  // open: clr
  Register #(.width(4)) R4 (.D(inpu), .en(demultiplexer_1_out4), .clk(clk), .Q(R4_q));  // open: clr
  Register #(.width(4)) R5 (.D(inpu), .en(demultiplexer_1_out5), .clk(clk), .Q(R5_q));  // open: clr
  Register #(.width(4)) R6 (.D(inpu), .en(demultiplexer_1_out6), .clk(clk), .Q(R6_q));  // open: clr
  Register #(.width(4)) R7 (.D(inpu), .en(demultiplexer_1_out7), .clk(clk), .Q(R7_q));  // open: clr
  Multiplexer #(.select(3), .width(4)) multiplexer_1 (
    .in0(R0_q), .in1(R1_q), .in2(R2_q), .in3(R3_q), .in4(R4_q), .in5(R5_q), .in6(R6_q), .in7(R7_q), .out(A),
    .sel(OutputRegAselect));
  Multiplexer #(.select(3), .width(4)) multiplexer_2 (
    .in0(R0_q), .in1(R1_q), .in2(R2_q), .in3(R3_q), .in4(R4_q), .in5(R5_q), .in6(R6_q), .in7(R7_q), .out(B),
    .sel(OutputRegBselect));
endmodule

module alu1 (
  input  [3:0] A,
  input  [3:0] B,
  input  [2:0] op,
  output [3:0] o
);

  wire [3:0] adder_1_out, and_1_out, or_1_out, subtractor_1_out, xor_1_out;

  assign and_1_out = A & B;  // AND_Gate and_1, 4 bits wide
  assign or_1_out = A | B;  // OR_Gate or_1, 4 bits wide
  Adder #(.width(4)) adder_1 (.a(A), .b(B), .out(adder_1_out));  // open: cin, cout
  Subtractor #(.width(4)) subtractor_1 (.a(A), .b(B), .out(subtractor_1_out));  // open: bin, bout
  assign xor_1_out = A ^ B;  // XOR_Gate xor_1, 4 bits wide
  Multiplexer #(.select(3), .width(4)) multiplexer_1 (
    .in0(adder_1_out), .in1(subtractor_1_out), .in2(and_1_out), .in3(or_1_out), .in4(xor_1_out), .out(o),
    .sel(op));  // open: in5, in6, in7
  Hex_Digit_Display hex_digit_display_1 (.value(o));  // open: dp

  // Notes on the sheet:
  //   000:+
  //   001:-
  //   010:AND
  //   011:OR
  //   100:XOR
endmodule
