// Logisim project regFile.circ as structural Verilog: 1 circuit, main circuit main
module main (
  input  [3:0] in_1,
  input  [2:0] in_2,
  input  [2:0] in_3,
  input  [2:0] in_4,
  output [3:0] out_5,
  output [3:0] out_6
);

  wire clock_1_out, demultiplexer_1_out0, demultiplexer_1_out1, demultiplexer_1_out2, demultiplexer_1_out3,
       demultiplexer_1_out4, demultiplexer_1_out5, demultiplexer_1_out6, demultiplexer_1_out7;
  wire [3:0] R0_q, R1_q, R2_q, R3_q, R4_q, R5_q, R6_q, R7_q;

  Clock clock_1 (.out(clock_1_out));
  Demultiplexer #(.select(3)) demultiplexer_1 (
    .out0(demultiplexer_1_out0), .out1(demultiplexer_1_out1), .out2(demultiplexer_1_out2),
    .out3(demultiplexer_1_out3), .out4(demultiplexer_1_out4), .out5(demultiplexer_1_out5),
    .out6(demultiplexer_1_out6), .out7(demultiplexer_1_out7), .in(1'b1), .sel(in_4));
  Register #(.width(4)) R0 (.D(in_1), .en(demultiplexer_1_out0), .clk(clock_1_out), .Q(R0_q));  // open: clr
  Register #(.width(4)) R1 (.D(in_1), .en(demultiplexer_1_out1), .clk(clock_1_out), .Q(R1_q));  // open: clr
  Register #(.width(4)) R2 (.D(in_1), .en(demultiplexer_1_out2), .clk(clock_1_out), .Q(R2_q));  // open: clr
  Register #(.width(4)) R3 (.D(in_1), .en(demultiplexer_1_out3), .clk(clock_1_out), .Q(R3_q));  // open: clr
  Register #(.width(4)) R4 (.D(in_1), .en(demultiplexer_1_out4), .clk(clock_1_out), .Q(R4_q));  // open: clr
  Register #(.width(4)) R5 (.D(in_1), .en(demultiplexer_1_out5), .clk(clock_1_out), .Q(R5_q));  // open: clr
  Register #(.width(4)) R6 (.D(in_1), .en(demultiplexer_1_out6), .clk(clock_1_out), .Q(R6_q));  // open: clr
  Register #(.width(4)) R7 (.D(in_1), .en(demultiplexer_1_out7), .clk(clock_1_out), .Q(R7_q));  // open: clr
  Multiplexer #(.select(3), .width(4)) multiplexer_1 (
    .in0(R0_q), .in1(R1_q), .in2(R2_q), .in3(R3_q), .in4(R4_q), .in5(R5_q), .in6(R6_q), .in7(R7_q),
    .out(out_5), .sel(in_2));
  Multiplexer #(.select(3), .width(4)) multiplexer_2 (
    .in0(R0_q), .in1(R1_q), .in2(R2_q), .in3(R3_q), .in4(R4_q), .in5(R5_q), .in6(R6_q), .in7(R7_q),
    .out(out_6), .sel(in_3));
endmodule
